# Fritzing sketch 1-Electricidad (saved by Fritzing 0.9.3b)
breadboards: 1

parts:
  R1 = Resistor [tolerance=±5% resistance=220 package=THT]
  LED1 = LED - 5mm [color="Red (633nm)" package="5 mm [THT]"]
  LED2 = LED - 5mm [color="Red (633nm)" package="5 mm [THT]"]
  LED3 = LED - 5mm [color="Red (633nm)" package="5 mm [THT]"]
  LED4 = LED - 5mm [color="Red (633nm)" package="5 mm [THT]"]
  JACK1 = 2.1mm Barrel Jack with Terminal Block
  LED5 = LED - 5mm [color="Red (633nm)" package="5 mm [THT]"]  # not connected

nets:
  N1: R1.Pin_0, JACK1.NEG
  N2: R1.Pin_1, LED1.cathode
  N3: LED1.anode, LED2.cathode
  N4: LED2.anode, LED3.cathode
  N5: LED3.anode, LED4.cathode
  N6: LED4.anode, JACK1.POS

notes:
  Alimentacion 12V
  - Negativa +Positiva
  Resistencia:
  * Roja
  * Roja
  * Marron
