# Fritzing sketch 3-Potenciometro (saved by Fritzing 0.9.3b)
breadboards: 1

parts:
  LED1 = LED - 5mm [color="Red (633nm)" package="5 mm [THT]"]
  LED2 = LED - 5mm [color="Red (633nm)" package="5 mm [THT]"]
  LED3 = LED - 5mm [color="Red (633nm)" package="5 mm [THT]"]
  LED4 = LED - 5mm [color="Red (633nm)" package="5 mm [THT]"]
  JACK1 = 2.1mm Barrel Jack with Terminal Block
  LED5 = LED - 5mm [color="Red (633nm)" package="5 mm [THT]"]  # not connected
  U2 = POT [package=alps_pot]

nets:
  N1: LED1.cathode, JACK1.NEG, U2.E, U2.A
  N2: LED1.anode, LED2.cathode
  N3: LED2.anode, LED3.cathode
  N4: LED3.anode, LED4.cathode
  N5: LED4.anode, U2.S

notes:
  Alimentacion 12V
  - Negativa +Positiva
